# Fritzing sketch led light (saved by Fritzing 0.9.3b)

parts:
  Часть1 = Arduino Nano (Rev3.0)
  Power_plug1 = Power plug
  S1 = H-Bridge with L298N
  LED1 = Super Flux RGB LED (com. anode)
  PIR1 = PIR sensor
  PIR2 = PIR sensor  # not connected
  PIR3 = PIR sensor  # not connected

nets:
  N1: Часть1.D3, S1.IN2
  N2: Часть1.D4, PIR1.SIG
  N3: Часть1.D5, S1.IN1
  N4: Часть1.D6, S1.IN3
  N5: Часть1.D9, S1.IN4
  VIN: Часть1.VIN, S1.5V
  GND: Power_plug1.GND, S1.GND, PIR1.GND
  VCC: Power_plug1.VCC, S1.12V
  N6: S1.M1-01, LED1.red_cathode
  N7: S1.M1-02, S1.M2-01, LED1.green_cathode
  N8: S1.M2-02, LED1.blue_cathode

custom parts:
  H-Bridge with L298N: h-bridge
